# Fritzing sketch NMEA_WiFi_Bridge (saved by Fritzing 0.9.1b)
stripboards: 1

parts:
  Espessif_Serial_Wifi_Modul_1 = ESP8266 ESP01 [part_number=ESP8266 package=THT]
  R1 = Resistor [tolerance=±5% resistance=4.7k package=THT]
  R2 = Resistor [tolerance=±5% resistance=4.7k package=THT]
  R3 = Resistor [tolerance=±5% resistance=4.7k package=THT]
  R4 = Resistor [tolerance=±5% resistance=4.7k package=THT]
  R5 = Resistor [tolerance=±5% resistance=4.7k package=THT]
  S1 = Pushbutton [part_number=config package=THT]
  S2 = Pushbutton [part_number=flash package=THT]
  S3 = Pushbutton [part_number=reset package=THT]
  Q1 = NPN-Transistor [part_number=2n2222 package="TO92 [THT]"]
  J1 = female pin header, 2 pins [form="♀ (female)" part_number=prgm]
  R6 = Resistor [tolerance=±5% resistance=10k package=THT]
  J2 = female pin header, 2 pins [form="♀ (female)" part_number=NMEA]
  R7 = Resistor [tolerance=±5% resistance=4.7k package=THT]
  U2 = V_REG_LD1117VXX [package=78xxl]
  C1 = Tantalum Capacitor [capacitance=1μF package="100 mil [THT, tantalum]"]
  J3 = female alternating pin header, 2 pins [form="♀ (female)" part_number=5v]
  R8 = Resistor [tolerance=±5% resistance=330 power=1 package=THT]
  D1 = Rectifier Diode [part_number=1N5819 package="300 mil [THT]"]
  LED1 = LED - 5mm [color="Yellow (585nm)" package="5 mm [THT]"]
  R9 = Resistor [tolerance=±5% resistance=270 package=THT]

nets:
  GND: Espessif_Serial_Wifi_Modul_1.GND, S2.leg0, S3.leg1, Q1.E, J2.pin2, U2.GND, C1.-, J3.pin1
  N1: Espessif_Serial_Wifi_Modul_1.RXD, R2.Pin_0, Q1.C, R7.Pin_0, D1.anode
  N2: Espessif_Serial_Wifi_Modul_1.TXD, R8.Pin_0
  N3: Espessif_Serial_Wifi_Modul_1.VCC, R1.Pin_1, R2.Pin_1, R3.Pin_1, R4.Pin_1, R5.Pin_1, R7.Pin_1, U2.OUT, C1.+, LED1.cathode
  N4: Espessif_Serial_Wifi_Modul_1.GPIO16, R5.Pin_0, S3.leg0
  N5: Espessif_Serial_Wifi_Modul_1.GPIO00, R3.Pin_0, S1.leg1, S2.leg1, R9.Pin_0
  N6: Espessif_Serial_Wifi_Modul_1.GPIO02, R1.Pin_0, S1.leg0
  N7: Espessif_Serial_Wifi_Modul_1.CH_PD, R4.Pin_0
  N8: Q1.B, R6.Pin_0
  N9: J1.pin1, D1.cathode
  N10: J1.pin2, R8.Pin_1
  N11: R6.Pin_1, J2.pin1
  N12: U2.IN, J3.pin2
  N13: LED1.anode, R9.Pin_1

notes:
  config
  flash
  <-reset
  Rx^ ^Tx
  NMEA in^
  GND^ ^+5v

custom parts:
  ESP8266 ESP01: Generic WiFi Module based on the ESP8266 with onboard PCB antenna and UART communications
